# Fritzing sketch keyboard-v2 (saved by Fritzing 0.9.3b)
circuit board: 28.4425cm x 8.91331cm
breadboards: 1

parts:
  Esc = Kailh Low Profile Switch [package=THT]
  F1 = Kailh Low Profile Switch [package=THT]
  F2 = Kailh Low Profile Switch [package=THT]
  F3 = Kailh Low Profile Switch [package=THT]
  F4 = Kailh Low Profile Switch [package=THT]
  F5 = Kailh Low Profile Switch [package=THT]
  F6 = Kailh Low Profile Switch [package=THT]
  F7 = Kailh Low Profile Switch [package=THT]
  F8 = Kailh Low Profile Switch [package=THT]
  F9 = Kailh Low Profile Switch [package=THT]
  F10 = Kailh Low Profile Switch [package=THT]
  F11 = Kailh Low Profile Switch [package=THT]
  Ins = Kailh Low Profile Switch [package=THT]
  Back = Kailh Low Profile Switch [package=THT]
  Tab = Kailh Low Profile Switch [package=THT]
  Q = Kailh Low Profile Switch [package=THT]
  W = Kailh Low Profile Switch [package=THT]
  ~ = Kailh Low Profile Switch [package=THT]
  Caps = Kailh Low Profile Switch [package=THT]
  A = Kailh Low Profile Switch [package=THT]
  Z = Kailh Low Profile Switch [package=THT]
  LShift = Kailh Low Profile Switch [package=THT]
  X = Kailh Low Profile Switch [package=THT]
  LCtrl = Kailh Low Profile Switch [package=THT]
  LAlt = Kailh Low Profile Switch [package=THT]
  Fn = Kailh Low Profile Switch [package=THT]
  C = Kailh Low Profile Switch [package=THT]
  V = Kailh Low Profile Switch [package=THT]
  Space = Kailh Low Profile Switch [package=THT]
  B = Kailh Low Profile Switch [package=THT]
  Del = Kailh Low Profile Switch [package=THT]
  PgUp = Kailh Low Profile Switch [package=THT]
  PgDn = Kailh Low Profile Switch [package=THT]
  Right = Kailh Low Profile Switch [package=THT]
  Down = Kailh Low Profile Switch [package=THT]
  Up = Kailh Low Profile Switch [package=THT]
  Left = Kailh Low Profile Switch [package=THT]
  F12 = Kailh Low Profile Switch [package=THT]
  E = Kailh Low Profile Switch [package=THT]
  R = Kailh Low Profile Switch [package=THT]
  T = Kailh Low Profile Switch [package=THT]
  Y = Kailh Low Profile Switch [package=THT]
  U = Kailh Low Profile Switch [package=THT]
  I = Kailh Low Profile Switch [package=THT]
  O = Kailh Low Profile Switch [package=THT]
  P = Kailh Low Profile Switch [package=THT]
  [ = Kailh Low Profile Switch [package=THT]
  ] = Kailh Low Profile Switch [package=THT]
  \ = Kailh Low Profile Switch [package=THT]
  RCtrl = Kailh Low Profile Switch [package=THT]
  Super = Kailh Low Profile Switch [package=THT]
  N = Kailh Low Profile Switch [package=THT]
  M = Kailh Low Profile Switch [package=THT]
  part = Kailh Low Profile Switch [package=THT]
  part_2 = Kailh Low Profile Switch [package=THT]
  / = Kailh Low Profile Switch [package=THT]
  RShift = Kailh Low Profile Switch [package=THT]
  S = Kailh Low Profile Switch [package=THT]
  D = Kailh Low Profile Switch [package=THT]
  F = Kailh Low Profile Switch [package=THT]
  G = Kailh Low Profile Switch [package=THT]
  H = Kailh Low Profile Switch [package=THT]
  J = Kailh Low Profile Switch [package=THT]
  K = Kailh Low Profile Switch [package=THT]
  L = Kailh Low Profile Switch [package=THT]
  ; = Kailh Low Profile Switch [package=THT]
  ' = Kailh Low Profile Switch [package=THT]
  Enter = Kailh Low Profile Switch [package=THT]
  RAlt = Kailh Low Profile Switch [package=THT]
  C3 = Ceramic Capacitor [capacitance=100nF package="0603 [SMD, multilayer]"]
  C4 = Ceramic Capacitor [capacitance=100nF package="0603 [SMD, multilayer]"]
  U3 = QFN-32 [chip_label=SAMD21 package=QFN]
  U4 = Voltage Regulator [package=sot23-5]
  Pad3 = Pad [width=2.6000000000000001 height=2.6000000000000001 connect=center]
  USB = mystery part, 4 pins [chip_label=?]
  SWIM = mystery part, 3 pins [chip_label=?]
  D29 = Rectifier Diode [package="Melf DO-213 AA [SMD]"]
  D30 = Rectifier Diode [package="Melf DO-213 AA [SMD]"]
  D31 = Rectifier Diode [package="Melf DO-213 AA [SMD]"]
  D32 = Rectifier Diode [package="Melf DO-213 AA [SMD]"]
  D33 = Rectifier Diode [package="Melf DO-213 AA [SMD]"]
  D34 = Rectifier Diode [package="Melf DO-213 AA [SMD]"]
  D35 = Rectifier Diode [package="Melf DO-213 AA [SMD]"]
  D36 = Rectifier Diode [package="Melf DO-213 AA [SMD]"]
  D37 = Rectifier Diode [package="Melf DO-213 AA [SMD]"]
  D38 = Rectifier Diode [package="Melf DO-213 AA [SMD]"]
  D39 = Rectifier Diode [package="Melf DO-213 AA [SMD]"]
  D40 = Rectifier Diode [package="Melf DO-213 AA [SMD]"]
  D41 = Rectifier Diode [package="Melf DO-213 AA [SMD]"]
  D42 = Rectifier Diode [package="Melf DO-213 AA [SMD]"]
  D43 = Rectifier Diode [package="Melf DO-213 AA [SMD]"]
  D44 = Rectifier Diode [package="Melf DO-213 AA [SMD]"]
  D45 = Rectifier Diode [package="Melf DO-213 AA [SMD]"]
  D46 = Rectifier Diode [package="Melf DO-213 AA [SMD]"]
  D47 = Rectifier Diode [package="Melf DO-213 AA [SMD]"]
  D48 = Rectifier Diode [package="Melf DO-213 AA [SMD]"]
  D49 = Rectifier Diode [package="Melf DO-213 AA [SMD]"]
  D50 = Rectifier Diode [package="Melf DO-213 AA [SMD]"]
  D51 = Rectifier Diode [package="Melf DO-213 AA [SMD]"]
  D52 = Rectifier Diode [package="Melf DO-213 AA [SMD]"]
  D53 = Rectifier Diode [package="Melf DO-213 AA [SMD]"]
  D54 = Rectifier Diode [package="Melf DO-213 AA [SMD]"]
  D55 = Rectifier Diode [package="Melf DO-213 AA [SMD]"]
  D56 = Rectifier Diode [package="Melf DO-213 AA [SMD]"]
  D57 = Rectifier Diode [package="Melf DO-213 AA [SMD]"]
  D58 = Rectifier Diode [package="Melf DO-213 AA [SMD]"]
  D59 = Rectifier Diode [package="Melf DO-213 AA [SMD]"]
  D60 = Rectifier Diode [package="Melf DO-213 AA [SMD]"]
  D61 = Rectifier Diode [package="Melf DO-213 AA [SMD]"]
  D62 = Rectifier Diode [package="Melf DO-213 AA [SMD]"]
  D63 = Rectifier Diode [package="Melf DO-213 AA [SMD]"]
  D64 = Rectifier Diode [package="Melf DO-213 AA [SMD]"]
  D65 = Rectifier Diode [package="Melf DO-213 AA [SMD]"]
  D66 = Rectifier Diode [package="Melf DO-213 AA [SMD]"]
  D67 = Rectifier Diode [package="Melf DO-213 AA [SMD]"]
  D68 = Rectifier Diode [package="Melf DO-213 AA [SMD]"]
  D69 = Rectifier Diode [package="Melf DO-213 AA [SMD]"]
  D70 = Rectifier Diode [package="Melf DO-213 AA [SMD]"]
  D71 = Rectifier Diode [package="Melf DO-213 AA [SMD]"]
  D72 = Rectifier Diode [package="Melf DO-213 AA [SMD]"]
  D73 = Rectifier Diode [package="Melf DO-213 AA [SMD]"]
  D74 = Rectifier Diode [package="Melf DO-213 AA [SMD]"]
  D75 = Rectifier Diode [package="Melf DO-213 AA [SMD]"]
  D76 = Rectifier Diode [package="Melf DO-213 AA [SMD]"]
  D77 = Rectifier Diode [package="Melf DO-213 AA [SMD]"]
  D78 = Rectifier Diode [package="Melf DO-213 AA [SMD]"]
  D79 = Rectifier Diode [package="Melf DO-213 AA [SMD]"]
  D80 = Rectifier Diode [package="Melf DO-213 AA [SMD]"]
  D81 = Rectifier Diode [package="Melf DO-213 AA [SMD]"]
  D82 = Rectifier Diode [package="Melf DO-213 AA [SMD]"]
  D83 = Rectifier Diode [package="Melf DO-213 AA [SMD]"]
  D84 = Rectifier Diode [package="Melf DO-213 AA [SMD]"]
  D85 = Rectifier Diode [package="Melf DO-213 AA [SMD]"]
  D86 = Rectifier Diode [package="Melf DO-213 AA [SMD]"]
  D87 = Rectifier Diode [package="Melf DO-213 AA [SMD]"]
  D88 = Rectifier Diode [package="Melf DO-213 AA [SMD]"]
  D89 = Rectifier Diode [package="Melf DO-213 AA [SMD]"]
  D90 = Rectifier Diode [package="Melf DO-213 AA [SMD]"]
  D91 = Rectifier Diode [package="Melf DO-213 AA [SMD]"]
  D92 = Rectifier Diode [package="Melf DO-213 AA [SMD]"]
  D93 = Rectifier Diode [package="Melf DO-213 AA [SMD]"]
  D94 = Rectifier Diode [package="Melf DO-213 AA [SMD]"]
  D95 = Rectifier Diode [package="Melf DO-213 AA [SMD]"]
  D96 = Rectifier Diode [package="Melf DO-213 AA [SMD]"]
  D97 = Rectifier Diode [package="Melf DO-213 AA [SMD]"]
  LED1 = smd LED [color="Red (633nm)" package="0805 [SMD]"]
  R1 = Resistor [tolerance=±5% resistance=220 package="0805 [SMD]"]

nets:
  N1: Esc.leg0, D42.anode
  N2: Esc.leg1, F1.leg1, Tab.leg1, ~.leg1, LCtrl.leg1, U3.8
  N3: F1.leg0, D41.anode
  N4: F2.leg0, D40.anode
  N5: F2.leg1, Q.leg1, Caps.leg1, A.leg1, LShift.leg1, U3.7
  N6: F3.leg0, D39.anode
  N7: F3.leg1, W.leg1, Z.leg1, Fn.leg1, S.leg1, U3.6
  N8: F4.leg0, D38.anode
  N9: F4.leg1, X.leg1, LAlt.leg1, E.leg1, D.leg1, U3.5
  N10: F5.leg0, D36.anode
  N11: F5.leg1, C.leg1, R.leg1, F.leg1, U3.4
  N12: F6.leg0, D35.anode
  N13: F6.leg1, V.leg1, Space.leg1, T.leg1, G.leg1, U3.17
  N14: F7.leg0, D34.anode
  N15: F7.leg1, B.leg1, Y.leg1, H.leg1, U3.16
  N16: F8.leg0, D33.anode
  N17: F8.leg1, U.leg1, N.leg1, J.leg1, U3.15
  N18: F9.leg0, D32.anode
  N19: F9.leg1, I.leg1, M.leg1, K.leg1, U3.14
  N20: F10.leg0, D31.anode
  N21: F10.leg1, O.leg1, part.leg1, L.leg1, RAlt.leg1, U3.13
  N22: F11.leg0, D30.anode
  N23: F11.leg1, P.leg1, Super.leg1, part_2.leg1, ;.leg1, U3.12
  N24: Ins.leg0, D57.anode
  N25: Ins.leg1, Del.leg1, PgUp.leg1, PgDn.leg1, Right.leg1, U3.25
  N26: Back.leg0, D37.anode
  N27: Back.leg1, Down.leg1, Up.leg1, \.leg1, Enter.leg1, U3.1
  N28: Tab.leg0, D43.anode
  N29: Q.leg0, D44.anode
  N30: W.leg0, D45.anode
  N31: ~.leg0, D75.anode
  N32: Caps.leg0, D74.anode
  N33: A.leg0, D73.anode
  N34: Z.leg0, D77.anode
  N35: LShift.leg0, D76.anode
  N36: X.leg0, D82.anode
  N37: LCtrl.leg0, D79.anode
  N38: LAlt.leg0, D78.anode
  N39: Fn.leg0, D80.anode
  N40: C.leg0, D83.anode
  N41: V.leg0, D84.anode
  N42: Space.leg0, D81.anode
  N43: B.leg0, D85.anode
  N44: Del.leg0, D58.anode
  N45: PgUp.leg0, D59.anode
  N46: PgDn.leg0, D60.anode
  N47: Right.leg0, D61.anode
  N48: Down.leg0, D95.anode
  N49: Up.leg0, D97.anode
  N50: Left.leg0, D94.anode
  N51: Left.leg1, ].leg1, RShift.leg1, U3.3
  N52: F12.leg0, D29.anode
  N53: F12.leg1, [.leg1, RCtrl.leg1, /.leg1, '.leg1, U3.11
  N54: E.leg0, D46.anode
  N55: R.leg0, D47.anode
  N56: T.leg0, D48.anode
  N57: Y.leg0, D49.anode
  N58: U.leg0, D50.anode
  N59: I.leg0, D51.anode
  N60: O.leg0, D52.anode
  N61: P.leg0, D53.anode
  N62: [.leg0, D54.anode
  N63: ].leg0, D55.anode
  N64: \.leg0, U3.2, D56.anode
  N65: RCtrl.leg0, D93.anode
  N66: Super.leg0, D91.anode
  N67: N.leg0, D86.anode
  N68: M.leg0, D88.anode
  N69: part.leg0, D89.anode
  N70: part_2.leg0, D90.anode
  N71: /.leg0, D92.anode
  N72: RShift.leg0, D96.anode
  N73: S.leg0, D72.anode
  N74: D.leg0, D71.anode
  N75: F.leg0, D70.anode
  N76: G.leg0, D69.anode
  N77: H.leg0, D68.anode
  N78: J.leg0, D67.anode
  N79: K.leg0, D66.anode
  N80: L.leg0, D65.anode
  N81: ;.leg0, D64.anode
  N82: '.leg0, D63.anode
  N83: Enter.leg0, D62.anode
  N84: RAlt.leg0, D87.anode
  N85: C3.0, U3.29
  N86: C3.1, C4.1, U3.10, U3.28, U4.GND, Pad3.pad, USB.pin1, LED1.cathode
  N87: C4.0, U3.9, U3.30, U4.OUT
  N88: U3.18, D61.cathode, D78.cathode, D79.cathode, D80.cathode, D81.cathode, D87.cathode, D91.cathode, D93.cathode, D94.cathode, D95.cathode
  N89: U3.19, D42.cathode, D60.cathode, D76.cathode, D77.cathode, D82.cathode, D83.cathode, D84.cathode, D85.cathode, D86.cathode, D88.cathode, D89.cathode, D90.cathode, D92.cathode, D96.cathode, D97.cathode
  N90: U3.20, D59.cathode, D62.cathode, D63.cathode, D64.cathode, D65.cathode, D66.cathode, D67.cathode, D68.cathode, D69.cathode, D70.cathode, D71.cathode, D72.cathode, D73.cathode, D74.cathode, D75.cathode
  N91: U3.21, D43.cathode, D44.cathode, D45.cathode, D46.cathode, D47.cathode, D48.cathode, D49.cathode, D50.cathode, D51.cathode, D52.cathode, D53.cathode, D54.cathode, D55.cathode, D56.cathode, D58.cathode
  N92: U3.22, D29.cathode, D30.cathode, D31.cathode, D32.cathode, D33.cathode, D34.cathode, D35.cathode, D36.cathode, D37.cathode, D38.cathode, D39.cathode, D40.cathode, D41.cathode, D57.cathode
  N93: U3.23, USB.pin3
  N94: U3.24, USB.pin2
  N95: U3.26, SWIM.pin1
  N96: U3.27, R1.Pin_0
  N97: U3.31, SWIM.pin3
  N98: U3.32, SWIM.pin2
  N99: U4.IN, U4.EN, USB.pin4
  N100: LED1.anode, R1.Pin_1

notes:
  Flounder Keyboard v1.0
  http://sheep.art.pl
  ↑ This way up. ↑

custom parts:
  Kailh Low Profile Switch: A generic pushbutton.
